// Logisim project 4 Bit Aritmathic.circ as structural Verilog: 1 circuit, main circuit main
module main (
  input  switch_subs_add,
  input  a1,
  input  b1,
  input  a2,
  input  b2,
  input  a3,
  input  b3
);

  wire and_1_out, and_2_out, and_3_out, and_4_out, and_5_out, and_6_out, and_7_out, and_8_out, and_9_out,
       and_10_out, and_11_out, and_12_out, and_13_out, B_nC_out, B_nCD_out, B_nD_out, C_nD_out, CD_out,
       nB_nD_out, nBC_out, nC_nD_out, not_1_out, not_2_out, not_3_out, not_4_out, not_5_out, or_1_out,
       or_2_out, or_3_out, or_4_out, or_5_out, or_6_out, or_7_out, or_8_out, or_9_out, or_10_out, or_11_out,
       or_12_out, xor_1_out, xor_2_out, xor_3_out, xor_4_out, xor_5_out, xor_6_out, xor_7_out, xor_8_out,
       xor_9_out, xor_10_out, xor_11_out, xor_12_out, xor_13_out, xor_14_out, xor_15_out, xor_16_out,
       xor_17_out, xor_18_out;

  xor xor_1 (xor_1_out, switch_subs_add, b1);
  xor xor_2 (xor_2_out, switch_subs_add, b2);
  xor xor_3 (xor_3_out, switch_subs_add, b3);
  xor xor_4 (xor_4_out, a1, xor_1_out);
  and and_1 (and_1_out, a1, xor_1_out);
  xor xor_5 (xor_5_out, a2, xor_2_out);
  and and_2 (and_2_out, a2, xor_2_out);
  xor xor_6 (xor_6_out, a3, xor_3_out);
  and and_3 (and_3_out, a3, xor_3_out);
  xor xor_7 (xor_7_out, xor_4_out, switch_subs_add);
  and and_4 (and_4_out, xor_4_out, switch_subs_add);
  xor xor_8 (xor_8_out, xor_5_out, or_1_out);
  and and_5 (and_5_out, xor_5_out, or_1_out);
  xor xor_9 (xor_9_out, xor_6_out, or_2_out);
  and and_6 (and_6_out, xor_6_out, or_2_out);
  or or_1 (or_1_out, and_4_out, and_1_out);
  or or_2 (or_2_out, and_5_out, and_2_out);
  or or_3 (or_3_out, and_6_out, and_3_out);
  not not_1 (not_1_out, or_3_out);
  xor xor_10 (xor_10_out, and_7_out, xor_7_out);
  xor xor_11 (xor_11_out, and_7_out, xor_8_out);
  xor xor_12 (xor_12_out, and_7_out, xor_9_out);
  and and_7 (and_7_out, not_1_out, switch_subs_add);
  LED led_1 (.in(and_7_out));
  xor xor_13 (xor_13_out, 1'b0, xor_10_out);
  xor xor_14 (xor_14_out, 1'b0, xor_11_out);
  xor xor_15 (xor_15_out, 1'b0, xor_12_out);
  xor xor_16 (xor_16_out, xor_13_out, and_7_out);
  and and_8 (and_8_out, xor_13_out, and_7_out);
  and and_9 (and_9_out, 1'b0, xor_10_out);
  xor xor_17 (xor_17_out, xor_14_out, or_4_out);
  and and_10 (and_10_out, xor_14_out, or_4_out);
  and and_11 (and_11_out, 1'b0, xor_11_out);
  xor xor_18 (xor_18_out, xor_15_out, or_5_out);
  not not_2 (not_2_out, switch_subs_add);
  or or_4 (or_4_out, and_8_out, and_9_out);
  or or_5 (or_5_out, and_10_out, and_11_out);
  and and_12 (and_12_out, or_3_out, not_2_out);
  LED led_2 (.in(and_12_out));
  LED led_3 (.in(xor_18_out));
  not not_3 (not_3_out, xor_18_out);
  LED led_4 (.in(xor_17_out));
  not not_4 (not_4_out, xor_17_out);
  LED led_5 (.in(xor_16_out));
  not not_5 (not_5_out, xor_16_out);
  and B_nC (B_nC_out, xor_18_out, not_4_out);
  and B_nD (B_nD_out, xor_18_out, not_5_out);
  and and_13 (and_13_out, xor_18_out, xor_16_out);
  and nB_nD (nB_nD_out, not_3_out, not_5_out);
  and CD (CD_out, xor_17_out, xor_16_out);
  and nC_nD (nC_nD_out, not_4_out, not_5_out);
  and C_nD (C_nD_out, not_5_out, xor_17_out);
  and nBC (nBC_out, xor_17_out, not_3_out);
  and B_nCD (B_nCD_out, xor_16_out, B_nC_out);
  or or_6 (or_6_out, and_12_out, and_13_out, nB_nD_out, xor_17_out);
  or or_7 (or_7_out, not_3_out, nC_nD_out, CD_out);
  or or_8 (or_8_out, xor_18_out, not_4_out, xor_16_out);
  or or_9 (or_9_out, and_12_out, nB_nD_out, C_nD_out, nBC_out, B_nCD_out);
  or or_10 (or_10_out, nB_nD_out, C_nD_out);
  or or_11 (or_11_out, and_12_out, B_nC_out, B_nD_out, nC_nD_out);
  or or_12 (or_12_out, and_12_out, B_nC_out, C_nD_out, nBC_out);
  _7_Segment_Display u_7_segment_display_1 (
    .g(or_12_out), .f(or_11_out), .a(or_6_out), .b(or_7_out), .e(or_10_out), .d(or_9_out), .c(or_8_out));  // open: dp

  // Notes on the sheet:
  //   Signed bit
  //   A
  //   B
  //   C
  //   D
  //   BD
endmodule
